// Logisim project datapath_alejandro.circ as structural Verilog: 24 circuits, main circuit ALU
module datapath (
  input  Clock,
  input  Reset
);

  wire alu_1_p5, and_1_out, controlunit_1_alusrc, controlunit_1_branch, controlunit_1_memread,
       controlunit_1_memtoreg, controlunit_1_memwrite, controlunit_1_reg2loc, controlunit_1_regwrite;
  wire [1:0] aluctrl_1_oper, controlunit_1_aluop0, immextend_1_p4;
  wire [4:0] reg2loc_1_regout;
  wire [8:0] instructionmemory_1_inst;
  wire [18:0] instructionmemory_1_inst_2;
  wire [25:0] instructionmemory_1_inst_3;
  wire [31:26] instructionmemory_1_inst_4;
  wire [63:0] alu_1_p4, alusrcmux_1_aluin, branchadder_1_target, datamemory_1_readdata, immextend_1_p5,
       pc_1_outt, pc_select_1_nextpc, pcadder_1_outt, registerfile_1_rdata1, registerfile_1_rdata2,
       writebackmux_1_regwritedata;

  // Probe on {instructionmemory_1_inst_4, instructionmemory_1_inst_3[25:24], instructionmemory_1_inst_2[18:16], instructionmemory_1_inst, instructionmemory_1_inst_2[6:0], instructionmemory_1_inst_3[4:0]}
  PC pc_1 (.inn(pc_select_1_nextpc), .clk(Reset), .rst(Clock), .outt(pc_1_outt));
  // Probe on pc_1_outt
  InstructionMemory instructionmemory_1 (
    .addr(pc_1_outt),
    .inst({instructionmemory_1_inst_4, instructionmemory_1_inst_3[25:24], instructionmemory_1_inst_2[18:16], instructionmemory_1_inst, instructionmemory_1_inst_2[6:0], instructionmemory_1_inst_3[4:0]}));
  // ImmExtend immextend_1: pin names not known; wires that end beside it: instructionmemory_1_inst, {instructionmemory_1_inst_2[18:16], instructionmemory_1_inst, instructionmemory_1_inst_2[6:0]}, {instructionmemory_1_inst_3[25:24], instructionmemory_1_inst_2[18:16], instructionmemory_1_inst, instructionmemory_1_inst_2[6:0], instructionmemory_1_inst_3[4:0]}, immextend_1_p4, immextend_1_p5
  BranchAdder branchadder_1 (.PC(pc_1_outt), .Imm(immextend_1_p5), .Target(branchadder_1_target));
  and and_1 (and_1_out, controlunit_1_branch, alu_1_p5);
  ControlUnit controlunit_1 (
    .OpCode({instructionmemory_1_inst_4, instructionmemory_1_inst_3[25:24], instructionmemory_1_inst_2[18:16]}),
    .Reg2Loc(controlunit_1_reg2loc), .ALUSrc(controlunit_1_alusrc), .MemtoReg(controlunit_1_memtoreg),
    .RegWrite(controlunit_1_regwrite), .MemRead(controlunit_1_memread), .MemWrite(controlunit_1_memwrite),
    .Branch(controlunit_1_branch), .ALUOp1(controlunit_1_aluop0[1]), .ALUOp0(controlunit_1_aluop0[0]),
    .SignExtCtl(immextend_1_p4));
  Reg2Loc reg2loc_1 (
    .Reg20_16(instructionmemory_1_inst[8:4]), .Reg4_0(instructionmemory_1_inst_3[4:0]),
    .Reg2Locc(controlunit_1_reg2loc), .RegOut(reg2loc_1_regout));
  // Probe on instructionmemory_1_inst_2[4:0]
  // Probe on instructionmemory_1_inst_3[4:0]
  // Probe on reg2loc_1_regout
  // Probe on writebackmux_1_regwritedata
  WriteBackMux writebackmux_1 (
    .ALUResult(alu_1_p4), .MemData(datamemory_1_readdata), .Mem2Reg(controlunit_1_memtoreg),
    .RegWriteData(writebackmux_1_regwritedata));
  // Probe on datamemory_1_readdata
  // Probe on registerfile_1_rdata2
  PCAdder pcadder_1 (.inn(pc_1_outt), .outt(pcadder_1_outt));
  RegisterFile registerfile_1 (
    .ReadReg1(instructionmemory_1_inst_2[4:0]), .ReadReg2(reg2loc_1_regout),
    .WriteReg(instructionmemory_1_inst_3[4:0]), .RegWrite(controlunit_1_regwrite), .Clk(Clock),
    .WriteData(writebackmux_1_regwritedata), .rData1(registerfile_1_rdata1), .rData2(registerfile_1_rdata2));
  // Probe on controlunit_1_alusrc
  DataMemory datamemory_1 (
    .Address(alu_1_p4), .WriteData(registerfile_1_rdata2), .MemRead(controlunit_1_memread),
    .MemWrite(controlunit_1_memwrite), .Clock(Clock), .ReadData(datamemory_1_readdata));
  // Probe on {instructionmemory_1_inst_4, instructionmemory_1_inst_3[25:24], instructionmemory_1_inst_2[18:16]}
  // Probe on registerfile_1_rdata1
  PC_Select pc_select_1 (
    .PCPlus4(pcadder_1_outt), .BranchTarget(branchadder_1_target), .PCSrc(and_1_out),
    .NextPC(pc_select_1_nextpc));
  ALUCtrl aluctrl_1 (
    .aluop(controlunit_1_aluop0),
    .op({instructionmemory_1_inst_4, instructionmemory_1_inst_3[25:24], instructionmemory_1_inst_2[18:16]}),
    .oper(aluctrl_1_oper));
  // Probe on aluctrl_1_oper
  // Probe on alusrcmux_1_aluin
  ALUSrcMUX alusrcmux_1 (
    .RegData(registerfile_1_rdata2), .ImmData(immextend_1_p5), .ALUSrc(controlunit_1_alusrc),
    .ALUIn(alusrcmux_1_aluin));
  // Probe on alu_1_p4
  // ALU alu_1: pin names not known; wires that end beside it: registerfile_1_rdata1, alusrcmux_1_aluin, aluctrl_1_oper, alu_1_p4, alu_1_p5
endmodule

module ALU (
  input  [1:0] cnt,
  input  [63:0] a1,
  input  [63:0] a2,
  output [63:0] result,
  output zeroes
);

  wire [63:0] adder_1_out, adder_2_out, and_1_out, not_1_out, or_1_out;

  assign not_1_out = ~a2;  // NOT_Gate not_1, 64 bits wide
  assign and_1_out = a1 & a2;  // AND_Gate and_1, 64 bits wide
  Adder #(.width(64)) adder_1 (.a(a1), .b(not_1_out), .out(adder_1_out), .cin(1'b1));  // open: cout
  Adder #(.width(64)) adder_2 (.a(a1), .b(a2), .out(adder_2_out));  // open: cin, cout
  assign or_1_out = a1 | a2;  // OR_Gate or_1, 64 bits wide
  Multiplexer #(.select(2), .width(64)) multiplexer_1 (
    .in0(adder_2_out), .in1(adder_1_out), .in2(and_1_out), .in3(or_1_out), .out(result), .sel(cnt));
  Comparator #(.mode("unsigned"), .width(64)) comparator_1 (.a(result), .b({64{1'b0}}), .eq(zeroes));  // open: gt, lt
endmodule

module RegisterFile (
  input  [4:0] ReadReg1,
  input  [4:0] ReadReg2,
  input  [4:0] WriteReg,
  input  RegWrite,
  input  Clk,
  input  [63:0] WriteData,
  output [63:0] rData1,
  output [63:0] rData2
);

  wire [4:0] multiplexer_1_out, multiplexer_2_out;

  Multiplexer #(.width(5)) multiplexer_1 (.in0(ReadReg1), .in1(WriteReg), .out(multiplexer_1_out), .sel(RegWrite));
  RAM #(.addrWidth(5), .asyncread("true"), .dataWidth(64)) ram_1 (
    .addr(multiplexer_1_out), .we(RegWrite), .clk(Clk), .din(WriteData), .dout(rData1));  // open: oe
  Multiplexer #(.width(5)) multiplexer_2 (.in0(ReadReg2), .in1(WriteReg), .out(multiplexer_2_out), .sel(RegWrite));
  RAM #(.addrWidth(5), .asyncread("true"), .dataWidth(64)) RAM2 (
    .addr(multiplexer_2_out), .we(RegWrite), .clk(Clk), .din(WriteData), .dout(rData2));  // open: oe
endmodule

module ControlUnit (
  input  [10:0] OpCode,
  output Reg2Loc,
  output ALUSrc,
  output MemtoReg,
  output RegWrite,
  output MemRead,
  output MemWrite,
  output Branch,
  output ALUOp1,
  output ALUOp0,
  output [1:0] SignExtCtl
);

  wire ADDdec_add, ANDdec_andd, ORRdec_itsor, SUBdec_sub;

  decodeADD ADDdec (.op(OpCode), .Add(ADDdec_add));
  decodeSUB SUBdec (.op(OpCode), .Sub(SUBdec_sub));
  decodeLDUR LDURdec (.op(OpCode), .LDURR(MemRead));
  decodeSTUR STURdec (.op(OpCode), .STURR(MemWrite));
  decodeCBZ CBZdec (.OP(OpCode), .CBZ(ALUOp0));
  decodeORR ORRdec (.op(OpCode), .itsOR(ORRdec_itsor));
  decodeAND ANDdec (.op(OpCode), .ANDD(ANDdec_andd));
  decodeB Bdec (.op(OpCode), .BR(SignExtCtl[1]));
  or or_1 (Reg2Loc, MemWrite, ALUOp0);
  or or_2 (ALUSrc, MemWrite, MemRead);
  or or_3 (RegWrite, ADDdec_add, SUBdec_sub, ORRdec_itsor, ANDdec_andd, MemRead);
  or or_4 (Branch, SignExtCtl[1], ALUOp0);
  or or_5 (ALUOp1, ADDdec_add, SUBdec_sub, ORRdec_itsor, ANDdec_andd);

  assign MemtoReg = MemRead;
  assign SignExtCtl[0] = ALUOp0;
endmodule

module decodeADD (
  input  [10:0] op,
  output Add
);

  and and_1 (Add, ~op[0], ~op[1], ~op[2], op[3], op[4], ~op[5], op[6], ~op[7], ~op[8], ~op[9], op[10]);  // AND_Gate
endmodule

module decodeSUB (
  input  [10:0] op,
  output Sub
);

  and and_1 (Sub, ~op[0], ~op[1], ~op[2], op[3], op[4], ~op[5], op[6], ~op[7], ~op[8], op[9], op[10]);  // AND_Gate
endmodule

module decodeLDUR (
  input  [10:0] op,
  output LDURR
);

  and and_1 (LDURR, ~op[0], op[1], ~op[2], ~op[3], ~op[4], ~op[5], op[6], op[7], op[8], op[9], op[10]);  // AND_Gate
endmodule

module decodeSTUR (
  input  [10:0] op,
  output STURR
);

  and and_1 (STURR, ~op[0], ~op[1], ~op[2], ~op[3], ~op[4], ~op[5], op[6], op[7], op[8], op[9], op[10]);  // AND_Gate
endmodule

module decodeCBZ (
  input  [10:0] OP,
  output CBZ
);

  and and_1 (CBZ, ~OP[3], ~OP[4], OP[5], ~OP[6], OP[7], OP[8], ~OP[9], OP[10]);  // AND_Gate
endmodule

module decodeORR (
  input  [10:0] op,
  output itsOR
);

  and and_1 (itsOR, ~op[0], ~op[1], ~op[2], ~op[3], op[4], ~op[5], op[6], ~op[7], op[8], ~op[9], op[10]);  // AND_Gate
endmodule

module decodeAND (
  input  [10:0] op,
  output ANDD
);

  and and_1 (ANDD, ~op[0], ~op[1], ~op[2], ~op[3], op[4], ~op[5], op[6], ~op[7], ~op[8], ~op[9], op[10]);  // AND_Gate
endmodule

module decodeB (
  input  [10:0] op,
  output BR
);

  and and_1 (BR, op[5], ~op[6], op[7], ~op[8], ~op[9], ~op[10]);  // AND_Gate
endmodule

module ALUCtrl (
  input  [1:0] aluop,
  input  [10:0] op,
  output [1:0] oper
);

  wire and_1_out, and_2_out, and_3_out;
  wire [1:0] multiplexer_1_out, or_2_out;

  and and_1 (and_1_out, op[9], op[8], ~op[8]);  // AND_Gate
  or or_1 (or_2_out[1], and_3_out, op[8]);
  Multiplexer #(.select(2), .width(2)) multiplexer_1 (
    .in0(2'b00), .in1(2'b01), .in2(2'b10), .in3(2'b11), .out(multiplexer_1_out), .sel(or_2_out));
  Multiplexer #(.select(2), .width(2)) multiplexer_2 (
    .in0(2'b00), .in1(2'b01), .in2(multiplexer_1_out), .in3(2'b11), .out(oper), .sel(aluop));
  or or_2 (or_2_out[0], and_1_out, and_2_out);
  and and_2 (and_2_out, ~op[9], ~op[8], op[8]);  // AND_Gate
  and and_3 (and_3_out, ~op[8], ~op[8], ~op[9]);  // AND_Gate

  assign op[3] = op[8];
endmodule

module InstructionMemory (
  input  [63:0] addr,
  output [31:0] inst
);

  ROM #(.dataWidth(32)) rom_1 (.addr(addr[9:2]), .data(inst));

  // Notes on the sheet:
  //   contents of rom_1 (hex, n*v repeats v):
  //   f8400142 f8401143 cb020064 8b020065 b4000041 f80010e4 f8401143 8b010008
endmodule

module DataMemory (
  input  [63:0] Address,
  input  [63:0] WriteData,
  input  MemRead,
  input  MemWrite,
  input  Clock,
  output [63:0] ReadData
);

  RAM #(.asyncread("true"), .dataWidth(64)) ram_1 (
    .addr(Address[9:2]), .we(MemWrite), .oe(MemRead), .clk(Clock), .din(WriteData), .dout(ReadData));
endmodule

module PC (
  input  [63:0] inn,
  input  clk,
  input  rst,
  output [63:0] outt
);

  Register #(.width(64)) register_1 (.D(inn), .clk(clk), .Q(outt), .clr(rst));  // open: en
endmodule

module PCAdder (
  input  [63:0] inn,
  output [63:0] outt
);

  Adder #(.width(64)) adder_1 (.a(inn), .b(64'h4), .out(outt));  // open: cin, cout
endmodule

module ImmExtend (
  input  [1:0] sel,
  input  [8:0] D_imm,
  input  [18:0] CB_imm,
  input  [25:0] B_imm,
  output [63:0] extension
);

  wire [63:0] bit_extender_1_out, bit_extender_2_out, bit_extender_3_out;

  assign bit_extender_1_out = {{45{CB_imm[18]}}, CB_imm};  // Bit_Extender bit_extender_1
  assign bit_extender_2_out = {{38{B_imm[25]}}, B_imm};  // Bit_Extender bit_extender_2
  assign bit_extender_3_out = {{55{D_imm[8]}}, D_imm};  // Bit_Extender bit_extender_3
  Multiplexer #(.select(2), .width(64)) multiplexer_1 (
    .in0(bit_extender_3_out), .in1(bit_extender_1_out), .in2(bit_extender_2_out), .out(extension), .sel(sel));  // open: in3
endmodule

module BranchAdder (
  input  [63:0] PC,
  input  [63:0] Imm,
  output [63:0] Target
);

  Adder #(.width(64)) adder_1 (.a(PC), .b(Imm), .out(Target));  // open: cin, cout
endmodule

module Reg2Loc (
  input  [4:0] Reg20_16,
  input  [4:0] Reg4_0,
  input  Reg2Locc,
  output [4:0] RegOut
);

  Multiplexer #(.width(5)) multiplexer_1 (.in0(Reg20_16), .in1(Reg4_0), .out(RegOut), .sel(Reg2Locc));
endmodule

module ALUSrcMUX (
  input  [63:0] RegData,
  input  [63:0] ImmData,
  input  ALUSrc,
  output [63:0] ALUIn
);

  Multiplexer #(.width(64)) multiplexer_1 (.in0(RegData), .in1(ImmData), .out(ALUIn), .sel(ALUSrc));
endmodule

module WriteBackMux (
  input  [63:0] ALUResult,
  input  [63:0] MemData,
  input  Mem2Reg,
  output [63:0] RegWriteData
);

  Multiplexer #(.width(64)) multiplexer_1 (.in0(ALUResult), .in1(MemData), .out(RegWriteData), .sel(Mem2Reg));
endmodule

module PC_Select (
  input  [63:0] PCPlus4,
  input  [63:0] BranchTarget,
  input  PCSrc,
  output [63:0] NextPC
);

  Multiplexer #(.width(64)) multiplexer_1 (.in0(PCPlus4), .in1(BranchTarget), .out(NextPC), .sel(PCSrc));
endmodule

module BranchUnit (
  input  Branch,
  input  Zero,
  output src
);

  and and_1 (src, Branch, Zero);
endmodule
